# Fritzing sketch Russeleds (saved by Fritzing 0.9.3b)
breadboards: 1

parts:
  WeMos_D1_Mini1 = WeMos D1 Mini
  Part2 = Bluetooth HC-05 Macho
  IR1 = TSOP312.., 314.. [package=THT]
  HLK-PM1 = HLK-PM12 [part_number=HLK-PM12]
  LED4 = RGB LED (com. anode, rbg) [package="5 mm [THT]"]
  LED5 = RGB LED (com. anode, rbg) [package="5 mm [THT]"]
  LED6 = RGB LED (com. anode, rbg) [package="5 mm [THT]"]
  LED7 = RGB LED (com. anode, rbg) [package="5 mm [THT]"]

nets:
  5V: WeMos_D1_Mini1.5V, Part2.VCC, IR1.Vs
  N1: WeMos_D1_Mini1.D4, IR1.Data
  GND: WeMos_D1_Mini1.G, Part2.GND, IR1.GND, HLK-PM1.-Vo
  N2: WeMos_D1_Mini1.RX, Part2.TXD
  N3: WeMos_D1_Mini1.TX, Part2.RXD
  N4: HLK-PM1.+Vo, LED4.common_anode, LED5.common_anode, LED6.common_anode, LED7.common_anode
